# Fritzing sketch FinalProjectPart3F (saved by Fritzing 0.9.3b)
breadboards: 1

parts:
  Part2 = Arduino Uno (Rev3) - ICSP
  Disp3 = LBT2088AH [part_number=LBT2088AH]
  Part3 = LilyPad Buzzer
  Part4 = Real Time Clock Module - DS1307 RTC Breakout Board
  LED1 = smd LED [color="Red (633nm)" package="0805 [SMD]"]
  R1 = Resistor [tolerance=±5% resistance=220 package="1206 [SMD]"]
  R2 = Resistor [tolerance=±5% resistance=220 package="1206 [SMD]"]
  LED2 = LED - 5mm [color="Red (633nm)" package="5 mm [THT]"]
  Part5 = Color Sensor Breakout ADJD-S311

nets:
  N1: Part2.A4/SDA, Part4.SDA, Part5.SDA
  N2: Part2.A5/SCL, Part4.SCL, Part5.SCL
  GND: Part2.GND, Disp3.pin_16, Part3.-, Part4.GND, LED2.anode, Part5.GND
  N3: Part2.D2, Part4.SQW
  N4: Part2.D3_PWM, Disp3.pin_13
  N5: Part2.D4, Disp3.pin_14
  N6: Part2.D5_PWM, Disp3.pin_15
  N7: Part2.D6_PWM, R1.Pin_0
  N8: Part2.D7, Part5.LED
  3V3: Part2.3V3, Part5.VCC
  5V: Part2.5V, Disp3.pin_11, Part3.+, Part4.5V, R2.Pin_0
  N9: LED1.cathode, R1.Pin_1
  N10: R2.Pin_1, LED2.cathode
