# Fritzing sketch Homework 5 Sketch (saved by Fritzing 0.9.3b)
breadboards: 1

parts:
  Disp2 = LBT2088AH [part_number=LBT2088AH]
  R1 = Resistor [tolerance=±5% resistance=330 package=THT]
  LED1 = smd LED [color="Red (633nm)" package="0805 [SMD]"]  # not connected
  Part1 = Arduino Uno (Rev3) - ICSP
  Part2 = LilyPad Buzzer

nets:
  N1: Disp2.pin_4, Part1.D13/SCK
  N2: Disp2.pin_5, Part1.ICSP_MISO, Part1.D12/MISO
  N3: Disp2.pin_6, Part1.D11_PWM/MOSI
  N4: Disp2.pin_8, Part1.5V
  N5: R1.Pin_0, Part1.D8
  N6: Part1.A0, Part2.+
  N7: Part1.GND, Part2.-
